// Logisim project NPC.circ as structural Verilog: 1 circuit, main circuit main
// NPC
module main (
  input  CQ_PASSED,
  input  [31:0] INSTRUCTION,
  input  [23:0] CURRENT_PC,
  input  [23:0] JUMP_ADDRESS,
  output [23:0] NEXT_PC
);

  wire clk, Jump_Cmd, prev_jump, register_1_q;
  wire [31:0] current_inst, inst;

  Register #(.width(1)) register_1 (.D(Jump_Cmd), .Q(register_1_q), .clk(clk));  // open: en, clr
  not not_1 (prev_jump, register_1_q);
  Register #(.width(32)) Instruction_Register (.D(inst), .Q(current_inst), .clk(clk));  // open: en, clr

  // Notes on the sheet:
  //   NPC MODULE
endmodule
